# Fritzing sketch test_rtc-DS1302 (saved by Fritzing 0.9.3b)
breadboards: 2

parts:
  LED2 = 7-SEGMENT-4DIGIT-YOUNGSUN [package=7-segment-4digit-youngsun]
  U2 = 74HC595 SMD [package="SO16 [SMD]"]
  R4 = Resistor [tolerance=±5% resistance=220 package=THT]
  Част2 = Arduino Nano (Rev3.0)
  MH-Real-Time_Clock_Module_3 = RTC_DS1302_module
  R5 = Resistor [tolerance=±5% resistance=220 package=THT]
  R6 = Resistor [tolerance=±5% resistance=220 package=THT]
  R7 = Resistor [tolerance=±5% resistance=220 package=THT]

nets:
  N1: LED2.DIG1, U2.Q4
  N2: LED2.DIG2, U2.Q3
  N3: LED2.D, U2.Q7
  N4: LED2.COL-A, U2.Q2
  N5: LED2.E, U2.Q6
  N6: LED2.DIG3, R4.Pin_1
  N7: LED2.F, U2.Q1
  N8: LED2.COL-C, R7.Pin_1
  N9: LED2.A, U2.Q5
  N10: LED2.G, U2.Q0
  N11: LED2.B, R5.Pin_1
  N12: U2.MR, U2.VCC
  N13: U2.SH_CP, U2.DS, Част2.D6
  N14: U2.ST_CP, Част2.D5
  N15: R4.Pin_0, Част2.D9
  GND: Част2.GND, MH-Real-Time_Clock_Module_3.GND
  N16: Част2.D2, Част2.D3, Част2.D7, MH-Real-Time_Clock_Module_3.RST, MH-Real-Time_Clock_Module_3.DAT, MH-Real-Time_Clock_Module_3.CLK
  N17: Част2.D10, R7.Pin_0
  N18: Част2.D11/MOSI, R6.Pin_0
  N19: Част2.D12/MISO, R5.Pin_0
  3V3: Част2.3V3, MH-Real-Time_Clock_Module_3.VCC

custom parts:
  RTC_DS1302_module: Arduino module DS1302 SPI Real Time Clock
